// Logisim project 4 x 2bits + adder.circ as structural Verilog: 2 circuits, main circuit main
module main (
  input  Node1,
  input  Node2,
  input  Node3,
  input  Node4,
  input  Multiplier1,
  input  Multiplier2,
  output MSB,
  output Bit3,
  output Bit2,
  output Bit1,
  output Bit3_2,
  output Bit2_2,
  output Bit1_2,
  output LSB
);

  and _1_2___1_4 (MSB, Node1, Multiplier1);
  and _1_2___2_4 (Bit3, Node2, Multiplier1);
  and _1_2___3_4 (Bit2, Node3, Multiplier1);
  and _1_2___4_4 (Bit1, Node4, Multiplier1);
  and _2_2___1_4 (Bit3, Node1, Multiplier2);
  and _2_2___2_4 (Bit2_2, Node2, Multiplier2);
  and _2_2___3_4 (Bit1, Node3, Multiplier2);
  and _2_2___4_4 (LSB, Node4, Multiplier2);

  assign Bit1_2 = Bit1;
  assign Bit3_2 = Bit3;
endmodule

module Adder (
);


  // Notes on the sheet:
  //   Legg sammen 2 bits! Husk overflow bit! Overflow bit går til bit+1& resten er value for bit.
endmodule
