// Logisim project Full_Adder_quad.circ as structural Verilog: 2 circuits, main circuit main
module main (
  input  in_1,
  input  in_2,
  input  in_3,
  input  in_4,
  input  in_5,
  input  in_6,
  input  in_7,
  input  in_8,
  input  in_9,
  output out_10,
  output out_11,
  output out_12,
  output out_13,
  output out_14
);

  wire full_adder_1_overflow, full_adder_2_overflow, full_adder_3_overflow;

  Full_Adder full_adder_1 (
    .in_1(in_1), .in_2(in_2), .Overflow_in(in_3), .out_4(out_10), .Overflow(full_adder_1_overflow));
  Full_Adder full_adder_2 (
    .in_1(full_adder_1_overflow), .in_2(in_4), .Overflow_in(in_5), .out_4(out_11),
    .Overflow(full_adder_2_overflow));
  Full_Adder full_adder_3 (
    .in_1(full_adder_2_overflow), .in_2(in_6), .Overflow_in(in_7), .out_4(out_12),
    .Overflow(full_adder_3_overflow));
  Full_Adder full_adder_4 (
    .in_1(full_adder_3_overflow), .in_2(in_8), .Overflow_in(in_9), .out_4(out_13), .Overflow(out_14));
endmodule

module Full_Adder (
  input  in_1,
  input  in_2,
  input  Overflow_in,
  output out_4,
  output Overflow
);

  wire nand_1_out, nand_2_out, xor_1_out;

  xor xor_1 (xor_1_out, in_1, Overflow_in);
  nand nand_1 (nand_1_out, in_1, Overflow_in);
  nand nand_2 (nand_2_out, xor_1_out, in_2);
  xor xor_2 (out_4, xor_1_out, in_2);
  nand nand_3 (Overflow, nand_2_out, nand_1_out);
endmodule
