// Logisim project Oblig1.circ as structural Verilog: 3 circuits, main circuit main
module main (
  input  [3:0] Input,
  input  Sign_Bit,
  input  [2:0] Shift,
  output [4:0] out_4
);

  Shift shift_1 (.Input(Input), .Sign_bit(Sign_Bit), .Shift(Shift), .Output(out_4));
endmodule

// Shifter
module Shift (
  input  [3:0] Input,
  input  Sign_bit,
  input  [2:0] Shift,
  output [4:0] Output
);

  Shifter #(.width(5)) shifter_1 (.in({Sign_bit, Input}), .\dist (Shift), .out(Output));
endmodule

module Adder (
  input  in_1,
  input  in_2,
  input  in_3,
  input  B3,
  input  A3,
  input  B2,
  input  A2,
  input  B1,
  input  A1,
  input  B0,
  input  A0,
  input  Sign_bit,
  output out_13,
  output out_14,
  output Out_4,
  output Out_3,
  output Out_2,
  output Out_1,
  output Out_0,
  output [4:0] out_20
);

  wire xor_1_out, xor_2_out, xor_3_out, xor_4_out;

  xor xor_1 (xor_1_out, B3, Sign_bit);
  xor xor_2 (xor_2_out, B2, Sign_bit);
  xor xor_3 (xor_3_out, B1, Sign_bit);
  xor xor_4 (xor_4_out, B0, Sign_bit);

  assign out_20 = {Out_4, Out_3, Out_2, Out_1, Out_0};
endmodule
