// Logisim project Oblig1_new.circ as structural Verilog: 5 circuits, main circuit main
module main (
  input  Sign_Bit,
  input  [3:0] Input,
  output [7:0] out_3
);

  wire adder_1_overflow, adder_2_overflow, full_adder_1_overflow;

  Adder adder_1 (.In_a(Input[0]), .In_b(Input[2]), .Out(out_3[3]), .Overflow(adder_1_overflow));
  Full_Adder full_adder_1 (
    .A(Input[1]), .C(adder_1_overflow), .B(Input[3]), .Out(out_3[4]), .Overflow(full_adder_1_overflow));
  Adder adder_2 (.In_a(Input[2]), .In_b(full_adder_1_overflow), .Out(out_3[5]), .Overflow(adder_2_overflow));
  Adder adder_3 (.In_a(adder_2_overflow), .In_b(Input[3]), .Out(out_3[6]), .Overflow(out_3[7]));

  assign out_3[2:0] = {Input[1:0], 1'b0};
endmodule

// F A
module Full_Adder (
  input  A,
  input  C,
  input  B,
  output Out,
  output Overflow
);

  wire and_1_out, and_2_out, xor_1_out;

  xor xor_1 (xor_1_out, A, B);
  and and_1 (and_1_out, A, B);
  and and_2 (and_2_out, xor_1_out, C);
  xor xor_2 (Out, xor_1_out, C);
  or or_1 (Overflow, and_2_out, and_1_out);
endmodule

module Adder (
  input  In_a,
  input  In_b,
  output Out,
  output Overflow
);

  wire xor_2_out, xor_3_out;

  xor xor_1 (Out, In_a, In_b);
  xor xor_2 (xor_2_out, Out, In_b);
  xor xor_3 (xor_3_out, Out, In_a);
  and and_1 (Overflow, xor_2_out, xor_3_out);
endmodule

module Negate (
  input  [7:0] Input,
  input  Sign_bit,
  output [8:0] Check,
  output [8:0] Out
);

  xor xor_1 (Check[0], Input[0], Sign_bit);
  xor xor_2 (Check[1], Input[1], Sign_bit);
  xor xor_3 (Check[2], Input[2], Sign_bit);
  xor xor_4 (Check[3], Input[3], Sign_bit);
  xor xor_5 (Check[4], Input[4], Sign_bit);
  xor xor_6 (Check[5], Input[5], Sign_bit);
  xor xor_7 (Check[6], Input[6], Sign_bit);
  xor xor_8 (Check[7], Input[7], Sign_bit);
  and and_1 (Check[8], Input[7], Sign_bit);
endmodule

module Negate_Adder (
  input  In_1,
  input  [7:0] In_2,
  output [8:0] Out
);

  wire adder_1_overflow, adder_2_overflow, adder_3_overflow, adder_4_overflow, adder_5_overflow,
       adder_6_overflow, adder_7_overflow;

  Adder adder_1 (.In_a(In_1), .In_b(In_2[0]), .Out(Out[0]), .Overflow(adder_1_overflow));
  Adder adder_2 (.In_a(adder_1_overflow), .In_b(In_2[1]), .Out(Out[1]), .Overflow(adder_2_overflow));
  Adder adder_3 (.In_a(adder_2_overflow), .In_b(In_2[2]), .Out(Out[2]), .Overflow(adder_3_overflow));
  Adder adder_4 (.In_a(adder_3_overflow), .In_b(In_2[3]), .Out(Out[3]), .Overflow(adder_4_overflow));
  Adder adder_5 (.In_a(adder_4_overflow), .In_b(In_2[4]), .Out(Out[4]), .Overflow(adder_5_overflow));
  Adder adder_6 (.In_a(adder_5_overflow), .In_b(In_2[5]), .Out(Out[5]), .Overflow(adder_6_overflow));
  Adder adder_7 (.In_a(adder_6_overflow), .In_b(In_2[6]), .Out(Out[6]), .Overflow(adder_7_overflow));
  Adder adder_8 (.In_a(adder_7_overflow), .In_b(In_2[7]), .Out(Out[7]), .Overflow(Out[8]));
endmodule
