// Logisim project Oblig_close1.circ as structural Verilog: 8 circuits, main circuit main
module main (
  input  [3:0] Input,
  input  Sign_Bit,
  output [4:0] out_3,
  output [8:0] Final_out,
  output [8:0] out_5
);

  wire adder_1_overflow, adder_2_overflow, half_adder_1_overflow, half_adder_2_overflow;
  wire [5:0] n5bit_adder_1_out, n5bit_adder_2_out;
  wire [6:0] n6bit_adder_1_out;

  Negate negate_1 (.Input(Input), .Sign_bit(Sign_Bit), .Out({out_3[4:2], Final_out[2:1]}));  // open: Check
  Half_Adder half_adder_1 (.In_a(Final_out[1]), .In_b(out_3[2]), .Out(Final_out[3]), .Overflow(half_adder_1_overflow));
  Adder adder_1 (
    .A(Final_out[2]), .C(half_adder_1_overflow), .B(out_3[3]), .Out(Final_out[4]), .Overflow(adder_1_overflow));
  Adder adder_2 (.A(out_3[2]), .C(adder_1_overflow), .B(out_3[4]), .Out(Final_out[5]), .Overflow(adder_2_overflow));
  Half_Adder half_adder_2 (
    .In_a(adder_2_overflow), .In_b(out_3[3]), .Out(Final_out[6]), .Overflow(half_adder_2_overflow));
  Half_Adder half_adder_3 (.In_a(half_adder_2_overflow), .In_b(out_3[4]), .Out(Final_out[7]), .Overflow(Final_out[8]));
  _5bit_Adder u_5bit_adder_1 (
    .In_1({out_3[4:2], Final_out[2:1]}), .In_2({out_3[4:2], Final_out[2:1]}), .Out(n5bit_adder_1_out));
  _5bit_Adder u_5bit_adder_2 (
    .In_1({out_3[4:2], Final_out[2:1]}), .In_2({out_3[4:2], Final_out[2:1]}), .Out(n5bit_adder_2_out));
  _6bit_Adder u_6bit_adder_1 (.In_1(n5bit_adder_1_out), .In_2(n5bit_adder_2_out), .Out(n6bit_adder_1_out));
  _7_5bit_Adder u_7_5bit_adder_1 (
    .In_5bit({out_3[4:2], Final_out[2:1]}), .In_7bit(n6bit_adder_1_out), .Out(out_5[8:1]));

  assign Final_out[0] = 1'b0;
  assign out_3[1:0] = Final_out[2:1];
  assign out_5[0] = 1'b0;
endmodule

// Neg
module Negate (
  input  [3:0] Input,
  input  Sign_bit,
  output [4:0] Check,
  output [4:0] Out
);

  xor xor_1 (Check[0], Input[0], Sign_bit);
  xor xor_2 (Check[1], Input[1], Sign_bit);
  xor xor_3 (Check[2], Input[2], Sign_bit);
  xor xor_4 (Check[3], Input[3], Sign_bit);
  and and_1 (Check[4], Input[3], Sign_bit);
  Negate_Adder negate_adder_1 (.In_1(Check), .In_2(Sign_bit), .Out(Out));
endmodule

// FA
module Adder (
  input  A,
  input  C,
  input  B,
  output Out,
  output Overflow
);

  wire and_1_out, and_2_out, xor_1_out;

  xor xor_1 (xor_1_out, A, B);
  and and_1 (and_1_out, A, B);
  and and_2 (and_2_out, xor_1_out, C);
  xor xor_2 (Out, xor_1_out, C);
  or or_1 (Overflow, and_2_out, and_1_out);
endmodule

// N A
module Negate_Adder (
  input  [4:0] In_1,
  input  In_2,
  output [4:0] Out
);

  wire adder_1_overflow, adder_2_overflow, adder_3_overflow, adder_4_overflow;

  Adder adder_1 (.A(In_1[0]), .C(1'b0), .B(In_2), .Out(Out[0]), .Overflow(adder_1_overflow));
  Adder adder_2 (.A(In_1[1]), .C(adder_1_overflow), .B(1'b0), .Out(Out[1]), .Overflow(adder_2_overflow));
  Adder adder_3 (.A(In_1[2]), .C(adder_2_overflow), .B(1'b0), .Out(Out[2]), .Overflow(adder_3_overflow));
  Adder adder_4 (.A(In_1[3]), .C(adder_3_overflow), .B(1'b0), .Out(Out[3]), .Overflow(adder_4_overflow));
  Adder adder_5 (.A(In_1[4]), .C(adder_4_overflow), .B(1'b0), .Out(Out[4]));  // open: Overflow
endmodule

// H A
module Half_Adder (
  input  In_a,
  input  In_b,
  output Out,
  output Overflow
);

  wire xor_2_out, xor_3_out;

  xor xor_1 (Out, In_a, In_b);
  xor xor_2 (xor_2_out, Out, In_b);
  xor xor_3 (xor_3_out, Out, In_a);
  and and_1 (Overflow, xor_2_out, xor_3_out);
endmodule

// A_5b
module _5bit_Adder (
  input  [4:0] In_1,
  input  [4:0] In_2,
  output [5:0] Out
);

  wire adder_1_overflow, adder_2_overflow, adder_3_overflow, half_adder_1_overflow;

  Half_Adder half_adder_1 (.In_a(In_1[0]), .In_b(In_2[0]), .Out(Out[0]), .Overflow(half_adder_1_overflow));
  Adder adder_1 (.A(In_1[1]), .C(half_adder_1_overflow), .B(In_2[1]), .Out(Out[1]), .Overflow(adder_1_overflow));
  Adder adder_2 (.A(In_1[2]), .C(adder_1_overflow), .B(In_2[2]), .Out(Out[2]), .Overflow(adder_2_overflow));
  Adder adder_3 (.A(In_1[3]), .C(adder_2_overflow), .B(In_2[3]), .Out(Out[3]), .Overflow(adder_3_overflow));
  Adder adder_4 (.A(In_1[4]), .C(adder_3_overflow), .B(In_2[4]), .Out(Out[4]), .Overflow(Out[5]));
endmodule

// A_6b
module _6bit_Adder (
  input  [5:0] In_1,
  input  [5:0] In_2,
  output [6:0] Out
);

  wire adder_1_overflow, adder_2_overflow, adder_3_overflow, adder_4_overflow, half_adder_1_overflow;

  Half_Adder half_adder_1 (.In_a(In_1[0]), .In_b(In_2[0]), .Out(Out[0]), .Overflow(half_adder_1_overflow));
  Adder adder_1 (.A(In_1[1]), .C(half_adder_1_overflow), .B(In_2[1]), .Out(Out[1]), .Overflow(adder_1_overflow));
  Adder adder_2 (.A(In_1[2]), .C(adder_1_overflow), .B(In_2[2]), .Out(Out[2]), .Overflow(adder_2_overflow));
  Adder adder_3 (.A(In_1[3]), .C(adder_2_overflow), .B(In_2[3]), .Out(Out[3]), .Overflow(adder_3_overflow));
  Adder adder_4 (.A(In_1[4]), .C(adder_3_overflow), .B(In_2[4]), .Out(Out[4]), .Overflow(adder_4_overflow));
  Adder adder_5 (.A(In_1[5]), .C(adder_4_overflow), .B(In_2[5]), .Out(Out[5]), .Overflow(Out[6]));
endmodule

// A_7+5
module _7_5bit_Adder (
  input  [4:0] In_5bit,
  input  [6:0] In_7bit,
  output [7:0] Out
);

  wire adder_1_overflow, adder_2_overflow, adder_3_overflow, adder_4_overflow, half_adder_1_overflow,
       half_adder_2_overflow;

  Half_Adder half_adder_1 (.In_a(In_5bit[0]), .In_b(In_7bit[0]), .Out(Out[0]), .Overflow(half_adder_1_overflow));
  Adder adder_1 (.A(In_5bit[1]), .C(half_adder_1_overflow), .B(In_7bit[1]), .Out(Out[1]), .Overflow(adder_1_overflow));
  Adder adder_2 (.A(In_5bit[2]), .C(adder_1_overflow), .B(In_7bit[2]), .Out(Out[2]), .Overflow(adder_2_overflow));
  Adder adder_3 (.A(In_5bit[3]), .C(adder_2_overflow), .B(In_7bit[3]), .Out(Out[3]), .Overflow(adder_3_overflow));
  Adder adder_4 (.A(In_5bit[4]), .C(adder_3_overflow), .B(In_7bit[4]), .Out(Out[4]), .Overflow(adder_4_overflow));
  Half_Adder half_adder_2 (.In_a(adder_4_overflow), .In_b(In_7bit[5]), .Out(Out[5]), .Overflow(half_adder_2_overflow));
  Half_Adder half_adder_3 (.In_a(half_adder_2_overflow), .In_b(In_7bit[6]), .Out(Out[6]), .Overflow(Out[7]));
endmodule
